# Fritzing sketch Receiver (saved by Fritzing 0.9.3b)

parts:
  Part1 = Adafruit RFM9x LoRa Radio [part_number="Adafruit #3072 and #3073"]
  Part3 = Arduino Uno (Rev3) - ICSP

nets:
  VIN: Part1.VIN, Part3.5V
  GND: Part1.GND, Part3.GND
  N1: Part1.EN, Part3.D10_PWM/SS
  N2: Part1.DIO0, Part3.D2
  N3: Part1.SCK, Part3.D13/SCK
  N4: Part1.MISO, Part3.ICSP_MISO, Part3.D12/MISO
  N5: Part1.MOSI, Part3.D11_PWM/MOSI
  N6: Part1.RST, Part3.D9_PWM

custom parts:
  Adafruit RFM9x LoRa Radio: Sending data over long distances is like magic, and now you can be a magician with this range of powerful and easy-to-use radio modules. Sure, sometimes you want to talk to a computer (a good time to use WiFi) or perhaps communicate with a Phone (choose Bluetooth Low Energy!) but what if you want to send data very far? Most WiFi, Bluetooth, Zigbee and other wireless chipsets use 2.4GHz, which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
