# Fritzing sketch Sender Sketch (saved by Fritzing 0.9.3b)
breadboards: 1

parts:
  Part1 = Adafruit RFM9x LoRa Radio [part_number="Adafruit #3072 and #3073"]
  Part3 = Arduino Uno (Rev3) - ICSP
  VCC1 = Battery
  Part4 = Adafruit BME280 [part_number="Adafruit #2652"]
  PART1 = SparkFun Soil Moisture Sensor [part_number=SEN-13322]

nets:
  VCC: Part1.VIN, Part3.5V, VCC1.+, Part4.VCC, PART1.VCC
  GND: Part1.GND, Part3.GND, VCC1.-, Part4.GND, PART1.GND
  N1: Part1.EN, Part3.D10_PWM/SS
  N2: Part1.DIO0, Part3.D2
  N3: Part1.SCK, Part3.D13/SCK
  N4: Part1.MISO, Part3.ICSP_MISO, Part3.D12/MISO
  N5: Part1.MOSI, Part3.D11_PWM/MOSI
  N6: Part1.RST, Part3.D9_PWM
  N7: Part3.A0, PART1.SIG
  N8: Part3.D8, Part4.SCK/SCL
  N9: Part3.D5_PWM, Part4.CS
  N10: Part3.D6_PWM, Part4.SDI/SDA
  N11: Part3.D7, Part4.SDO/ADR

custom parts:
  Adafruit RFM9x LoRa Radio: Sending data over long distances is like magic, and now you can be a magician with this range of powerful and easy-to-use radio modules. Sure, sometimes you want to talk to a computer (a good time to use WiFi) or perhaps communicate with a Phone (choose Bluetooth Low Energy!) but what if you want to send data very far? Most WiFi, Bluetooth, Zigbee and other wireless chipsets use 2.4GHz, which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
  Adafruit BME280: Bosch has stepped up their game with their new BME280 sensor, an environmental sensor with temperature, barometric pressure and humidity! This sensor is great for all sorts of indoor environmental sensing and can even be used in both I2C and SPI! This precision sensor from Bosch is the best low-cost sensing solution for measuring humidity with ±3% accuracy, barometric pressure with ±1 hPa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
  SparkFun Soil Moisture Sensor: The SparkFun Soil Moisture Sensor is a simple breakout for measuring the moisture in soil and similar materials.
